// Digital circuit ALU_completa_t.dig as structural Verilog
module ALU_completa_t (
  input  [3:0] A,
  input  [3:0] B,
  input  [1:0] OP,
  output C,
  output Z,
  output N,
  output V,
  output [3:0] S
);

  wire notconnected_1_out;

  Seven_Seg_Hex seven_seg_hex_1 (.d(S), .dp(notconnected_1_out));
  // NotConnected on notconnected_1_out
endmodule
