// Digital circuit complementadorA2_t.dig as structural Verilog
module complementadorA2_t (
  input  [3:0] B_2,
  input  Neg,
  output [3:0] B
);

  wire notconnected_1_out;

  Seven_Seg_Hex seven_seg_hex_1 (.d(B), .dp(notconnected_1_out));
  // NotConnected on notconnected_1_out
endmodule
