// Digital circuit sum_4bit_t.dig as structural Verilog
module sum_4bit_t (
  input  [3:0] A,
  input  [3:0] B,
  input  Cin,
  output [3:0] S,
  output Cout
);

  Seven_Seg_Hex seven_seg_hex_1 (.d(S), .dp(Cout));
endmodule
