// Digital circuit test1.dig as structural Verilog
module test1 (
  input  [2:0] A,
  input  [2:0] B,
  output [2:0] Y
);

  assign Y = A & B;  // And and_1, 3 bits wide
  LED led_1 (.in(Y[0]));
  LED led_2 (.in(Y[1]));
  LED led_3 (.in(Y[2]));
endmodule
