// Digital circuit unidad_aritmetica_t.dig as structural Verilog
module unidad_aritmetica_t (
  input  [3:0] A,
  input  [3:0] B,
  input  OP,
  output [3:0] S,
  output C,
  output Z,
  output N,
  output V
);

  wire notconnected_1_out;

  Seven_Seg_Hex seven_seg_hex_1 (.d({N, S[2:0]}), .dp(notconnected_1_out));
  // NotConnected on notconnected_1_out

  assign S[3] = N;
endmodule
